// Logisim project gpufinal.circ as structural Verilog: 16 circuits, main circuit Computer
module Computer (
);

  wire clock_1_out, clock_2_out, clock_3_out, cpu_1_buswriteenable, joycontrol_1_we_tobus, keyboard_1_avail,
       keyboardcontroller_1_keyboardread, keyboardcontroller_1_writetobus,
       memorycontroller_1_writeenabletomem, memorycontroller_1_writetobus, rgb_video_1_p1, rgb_video_1_p2,
       rgbcontroller_1_bus_we, terminalcontroller_1_writetoterminal, to7seg_1_bot, to7seg_1_botleft,
       to7seg_1_botright, to7seg_1_middle, to7seg_1_top, to7seg_1_topleft, to7seg_1_topright, to7seg_2_bot,
       to7seg_2_botleft, to7seg_2_botright, to7seg_2_middle, to7seg_2_top, to7seg_2_topleft,
       to7seg_2_topright, to7seg_3_bot, to7seg_3_botleft, to7seg_3_botright, to7seg_3_middle, to7seg_3_top,
       to7seg_3_topleft, to7seg_3_topright;
  wire [3:0] controller7seg_1_out_3, controller7seg_1_out_4, controller7seg_1_out_5;
  wire [6:0] keyboard_1_data, terminalcontroller_1_datatoterminal;
  wire [7:0] joystick_1_x, rgb_video_1_p3, rgb_video_1_p4;
  wire [14:0] adder_1_out, adder_2_out, adder_3_out, adder_4_out, adder_5_out, adder_6_out, adder_7_out,
       adder_8_out, adder_9_out, adder_10_out, adder_11_out, adder_12_out, adder_13_out, adder_14_out,
       adder_15_out, ledcontroller_1_out_3, ledcontroller_1_out_4, ledcontroller_1_out_5,
       ledcontroller_1_out_6, ledcontroller_1_out_7, ledcontroller_1_out_8, ledcontroller_1_out_9,
       ledcontroller_1_out_10, ledcontroller_1_out_11, ledcontroller_1_out_12, ledcontroller_1_out_13,
       ledcontroller_1_out_14, ledcontroller_1_out_15, ledcontroller_1_out_16, ledcontroller_1_out_17,
       matrixcontroller_1_out_4, matrixcontroller_1_out_5, matrixcontroller_1_out_6,
       matrixcontroller_1_out_7, matrixcontroller_1_out_8, matrixcontroller_1_out_9,
       matrixcontroller_1_out_10, matrixcontroller_1_out_11, matrixcontroller_1_out_12,
       matrixcontroller_1_out_13, matrixcontroller_1_out_14, matrixcontroller_1_out_15,
       matrixcontroller_1_out_16, matrixcontroller_1_out_17, matrixcontroller_1_out_18;
  wire [23:0] memorycontroller_1_addresstomem, rgb_video_1_p5;
  wire [25:0] cpu_1_addresstobus;
  wire [31:0] bit_extender_1_out, controlled_buffer_1_out, cpu_1_datatobus, joycontrol_1_data_tobus,
       keyboardcontroller_1_datatobus, memorycontroller_1_datatobus, memorycontroller_1_datatomem,
       ram_1_dout, rgbcontroller_1_data_tobus;

  Joystick joystick_1 (.x(joystick_1_x[3:0]), .y(joystick_1_x[7:4]));
  RAM #(.addrWidth(24), .dataWidth(32), .enables("line")) ram_1 (
    .addr(memorycontroller_1_addresstomem), .we(memorycontroller_1_writeenabletomem), .clk(clock_1_out),
    .din(memorycontroller_1_datatomem), .dout(ram_1_dout));
  Clock clock_1 (.out(clock_1_out));
  ledcontroller ledcontroller_1 (
    .in_1(joystick_1_x[3:0]), .in_2(joystick_1_x[7:4]), .out_3(ledcontroller_1_out_3),
    .out_4(ledcontroller_1_out_4), .out_5(ledcontroller_1_out_5), .out_6(ledcontroller_1_out_6),
    .out_7(ledcontroller_1_out_7), .out_8(ledcontroller_1_out_8), .out_9(ledcontroller_1_out_9),
    .out_10(ledcontroller_1_out_10), .out_11(ledcontroller_1_out_11), .out_12(ledcontroller_1_out_12),
    .out_13(ledcontroller_1_out_13), .out_14(ledcontroller_1_out_14), .out_15(ledcontroller_1_out_15),
    .out_16(ledcontroller_1_out_16), .out_17(ledcontroller_1_out_17));
  matrixcontroller matrixcontroller_1 (
    .WriteEnableFromBus(cpu_1_buswriteenable), .AddressFromBus(cpu_1_addresstobus),
    .DataFromBus(controlled_buffer_1_out), .out_4(matrixcontroller_1_out_4),
    .out_5(matrixcontroller_1_out_5), .out_6(matrixcontroller_1_out_6), .out_7(matrixcontroller_1_out_7),
    .out_8(matrixcontroller_1_out_8), .out_9(matrixcontroller_1_out_9), .out_10(matrixcontroller_1_out_10),
    .out_11(matrixcontroller_1_out_11), .out_12(matrixcontroller_1_out_12),
    .out_13(matrixcontroller_1_out_13), .out_14(matrixcontroller_1_out_14),
    .out_15(matrixcontroller_1_out_15), .out_16(matrixcontroller_1_out_16),
    .out_17(matrixcontroller_1_out_17), .out_18(matrixcontroller_1_out_18));
  assign bit_extender_1_out = {{24{1'b0}}, joystick_1_x};  // Bit_Extender bit_extender_1
  Adder #(.width(15)) adder_1 (
    .a(ledcontroller_1_out_3), .b(matrixcontroller_1_out_4), .out(adder_1_out));  // open: cin, cout
  Adder #(.width(15)) adder_2 (
    .a(ledcontroller_1_out_4), .b(matrixcontroller_1_out_5), .out(adder_2_out));  // open: cin, cout
  Adder #(.width(15)) adder_3 (
    .a(ledcontroller_1_out_5), .b(matrixcontroller_1_out_6), .out(adder_3_out));  // open: cin, cout
  Adder #(.width(15)) adder_4 (
    .a(ledcontroller_1_out_6), .b(matrixcontroller_1_out_7), .out(adder_4_out));  // open: cin, cout
  Adder #(.width(15)) adder_5 (
    .a(ledcontroller_1_out_7), .b(matrixcontroller_1_out_8), .out(adder_5_out));  // open: cin, cout
  Adder #(.width(15)) adder_6 (
    .a(ledcontroller_1_out_8), .b(matrixcontroller_1_out_9), .out(adder_6_out));  // open: cin, cout
  Adder #(.width(15)) adder_7 (
    .a(ledcontroller_1_out_9), .b(matrixcontroller_1_out_10), .out(adder_7_out));  // open: cin, cout
  Adder #(.width(15)) adder_8 (
    .a(ledcontroller_1_out_10), .b(matrixcontroller_1_out_11), .out(adder_8_out));  // open: cin, cout
  Adder #(.width(15)) adder_9 (
    .a(ledcontroller_1_out_11), .b(matrixcontroller_1_out_12), .out(adder_9_out));  // open: cin, cout
  Adder #(.width(15)) adder_10 (
    .a(ledcontroller_1_out_12), .b(matrixcontroller_1_out_13), .out(adder_10_out));  // open: cin, cout
  Adder #(.width(15)) adder_11 (
    .a(ledcontroller_1_out_13), .b(matrixcontroller_1_out_14), .out(adder_11_out));  // open: cin, cout
  Adder #(.width(15)) adder_12 (
    .a(ledcontroller_1_out_14), .b(matrixcontroller_1_out_15), .out(adder_12_out));  // open: cin, cout
  Adder #(.width(15)) adder_13 (
    .a(ledcontroller_1_out_15), .b(matrixcontroller_1_out_16), .out(adder_13_out));  // open: cin, cout
  Adder #(.width(15)) adder_14 (
    .a(ledcontroller_1_out_16), .b(matrixcontroller_1_out_17), .out(adder_14_out));  // open: cin, cout
  Adder #(.width(15)) adder_15 (
    .a(ledcontroller_1_out_17), .b(matrixcontroller_1_out_18), .out(adder_15_out));  // open: cin, cout
  Clock clock_2 (.out(clock_2_out));
  Keyboard keyboard_1 (
    .clk(clock_2_out), .re(keyboardcontroller_1_keyboardread), .avail(keyboard_1_avail),
    .data(keyboard_1_data));  // open: clr
  MemoryController memorycontroller_1 (
    .WriteEnableFromBus(cpu_1_buswriteenable), .AddressFromBus(cpu_1_addresstobus), .DataFromMem(ram_1_dout),
    .DataFromBus(controlled_buffer_1_out), .WriteEnableToMem(memorycontroller_1_writeenabletomem),
    .DataToBus(memorycontroller_1_datatobus), .AddressToMem(memorycontroller_1_addresstomem),
    .DataToMem(memorycontroller_1_datatomem), .WriteToBus(memorycontroller_1_writetobus));
  CPU cpu_1 (
    .DataFromBus(controlled_buffer_1_out), .BusWriteEnable(cpu_1_buswriteenable),
    .DataToBus(cpu_1_datatobus), .AddressToBus(cpu_1_addresstobus));
  DotMatrix #(.inputtype("row"), .matrixcols(15), .matrixrows(15)) dotmatrix_1 (
    .row0(adder_1_out), .row1(adder_2_out), .row2(adder_3_out), .row3(adder_4_out), .row4(adder_5_out),
    .row5(adder_6_out), .row6(adder_7_out), .row7(adder_8_out), .row8(adder_9_out), .row9(adder_10_out),
    .row10(adder_11_out), .row11(adder_12_out), .row12(adder_13_out), .row13(adder_14_out),
    .row14(adder_15_out));
  assign controlled_buffer_1_out = memorycontroller_1_writetobus ? memorycontroller_1_datatobus : 32'bz;  // Controlled_Buffer controlled_buffer_1
  assign controlled_buffer_1_out = cpu_1_buswriteenable ? cpu_1_datatobus : 32'bz;  // Controlled_Buffer controlled_buffer_2
  KeyboardController keyboardcontroller_1 (
    .KeyboardStatus(keyboard_1_avail), .WriteEnableFromBus(cpu_1_buswriteenable),
    .KeyboardData(keyboard_1_data), .DataFromBus(controlled_buffer_1_out),
    .AddressFromBus(cpu_1_addresstobus), .DataToBus(keyboardcontroller_1_datatobus),
    .WriteToBus(keyboardcontroller_1_writetobus), .KeyboardRead(keyboardcontroller_1_keyboardread));
  assign controlled_buffer_1_out = keyboardcontroller_1_writetobus ? keyboardcontroller_1_datatobus : 32'bz;  // Controlled_Buffer controlled_buffer_3
  assign controlled_buffer_1_out = joycontrol_1_we_tobus ? joycontrol_1_data_tobus : 32'bz;  // Controlled_Buffer controlled_buffer_4
  joycontrol joycontrol_1 (
    .address(cpu_1_addresstobus), .data(bit_extender_1_out), .data_tobus(joycontrol_1_data_tobus),
    .we_tobus(joycontrol_1_we_tobus));
  Clock clock_3 (.out(clock_3_out));
  TTY tty_1 (
    .data(terminalcontroller_1_datatoterminal), .clk(clock_3_out), .we(terminalcontroller_1_writetoterminal));  // open: clr
  // RGB_Video #(.height(256), .scale(1), .width(256)) rgb_video_1: pin names not known; wires that end beside it: rgb_video_1_p1, rgb_video_1_p2, rgb_video_1_p3, rgb_video_1_p4, rgb_video_1_p5
  Clock clock_4 (.out(rgb_video_1_p1));
  assign controlled_buffer_1_out = rgbcontroller_1_bus_we ? rgbcontroller_1_data_tobus : 32'bz;  // Controlled_Buffer controlled_buffer_5
  TerminalController terminalcontroller_1 (
    .WriteEnableFromBus(cpu_1_buswriteenable), .AddressFromBus(cpu_1_addresstobus),
    .DataFromBus(controlled_buffer_1_out), .DataToTerminal(terminalcontroller_1_datatoterminal),
    .WriteToTerminal(terminalcontroller_1_writetoterminal));
  RGBController rgbcontroller_1 (
    .AddressFromBus(cpu_1_addresstobus), .DataFromBus(controlled_buffer_1_out),
    .WriteEnable(cpu_1_buswriteenable), .RGBX(rgb_video_1_p3), .RGBY(rgb_video_1_p4),
    .RGBColor(rgb_video_1_p5), .RGBWrite(rgb_video_1_p2), .data_tobus(rgbcontroller_1_data_tobus),
    .bus_we(rgbcontroller_1_bus_we));
  controller7seg controller7seg_1 (
    .AddFromBus(cpu_1_addresstobus), .DataFromBus(controlled_buffer_1_out), .out_3(controller7seg_1_out_3),
    .out_4(controller7seg_1_out_4), .out_5(controller7seg_1_out_5));
  _7_Segment_Display u_7_segment_display_1 (
    .g(to7seg_1_middle), .f(to7seg_1_topleft), .a(to7seg_1_top), .b(to7seg_1_topright), .e(to7seg_1_botleft),
    .d(to7seg_1_bot), .c(to7seg_1_botright));  // open: dp
  to7seg to7seg_1 (
    .binnum(controller7seg_1_out_3), .top(to7seg_1_top), .topright(to7seg_1_topright),
    .botright(to7seg_1_botright), .bot(to7seg_1_bot), .botleft(to7seg_1_botleft), .topleft(to7seg_1_topleft),
    .middle(to7seg_1_middle));
  to7seg to7seg_2 (
    .binnum(controller7seg_1_out_4), .top(to7seg_2_top), .topright(to7seg_2_topright),
    .botright(to7seg_2_botright), .bot(to7seg_2_bot), .botleft(to7seg_2_botleft), .topleft(to7seg_2_topleft),
    .middle(to7seg_2_middle));
  to7seg to7seg_3 (
    .binnum(controller7seg_1_out_5), .top(to7seg_3_top), .topright(to7seg_3_topright),
    .botright(to7seg_3_botright), .bot(to7seg_3_bot), .botleft(to7seg_3_botleft), .topleft(to7seg_3_topleft),
    .middle(to7seg_3_middle));
  _7_Segment_Display u_7_segment_display_2 (
    .g(to7seg_2_middle), .f(to7seg_2_topleft), .a(to7seg_2_top), .b(to7seg_2_topright), .e(to7seg_2_botleft),
    .d(to7seg_2_bot), .c(to7seg_2_botright));  // open: dp
  _7_Segment_Display u_7_segment_display_3 (
    .g(to7seg_3_middle), .f(to7seg_3_topleft), .a(to7seg_3_top), .b(to7seg_3_topright), .e(to7seg_3_botleft),
    .d(to7seg_3_bot), .c(to7seg_3_botright));  // open: dp

  // Notes on the sheet:
  //   Write_enable
  //   Address
  //   Data
endmodule

module CPU (
  input  [31:0] DataFromBus,
  output [25:0] AddressToBus,
  output BusWriteEnable,
  output [31:0] DataToBus
);

  wire alu_1_regs_equal, and_1_out, and_2_out, and_3_out, clock_1_out, control_1_imm_sel, control_1_is_beq,
       control_1_is_bne, control_1_is_j1, control_1_is_j2, control_1_is_j3, control_1_is_lw,
       control_1_reg_write_e, or_1_out, or_2_out;
  wire [3:0] control_1_alu_code;
  wire [4:0] control_1_rd, control_1_rs, control_1_rt, multiplexer_5_out;
  wire [15:0] bit_extender_3_out;
  wire [25:0] bit_extender_1_out;
  wire [31:0] adder_1_out, adder_2_out, alu_1_res, bit_extender_2_out, control_1_imm, multiplexer_1_out,
       multiplexer_2_out, multiplexer_3_out, multiplexer_4_out, multiplexer_6_out, multiplexer_7_out,
       regfile_1_rs_data, register_1_q, rom_1_data, shifter_1_out, shifter_2_out, shifter_3_out;

  Adder #(.width(32)) adder_1 (.a(register_1_q), .b(32'h4), .out(adder_1_out));  // open: cin, cout
  Shifter #(.width(32)) shifter_1 (.in(control_1_imm), .\dist (5'b00010), .out(shifter_1_out));
  Adder #(.width(32)) adder_2 (.a(adder_1_out), .b(shifter_1_out), .out(adder_2_out));  // open: cin, cout
  Bit_Extender #(.in_width(32), .out_width(26), .\type ("zero")) bit_extender_1 (
    .in(rom_1_data), .out(bit_extender_1_out));
  assign bit_extender_2_out = {{6{1'b0}}, bit_extender_1_out};  // Bit_Extender bit_extender_2
  Multiplexer #(.width(32)) multiplexer_1 (
    .in0(adder_1_out), .in1(adder_2_out), .out(multiplexer_1_out), .sel(or_1_out));
  Shifter #(.width(32)) shifter_2 (.in(bit_extender_2_out), .\dist (5'b00010), .out(shifter_2_out));
  Multiplexer #(.width(32)) multiplexer_2 (
    .in0(multiplexer_1_out), .in1(multiplexer_3_out), .out(multiplexer_2_out), .sel(or_2_out));
  Multiplexer #(.width(32)) multiplexer_3 (
    .in0(regfile_1_rs_data), .in1(shifter_2_out), .out(multiplexer_3_out), .sel(control_1_is_j1));
  or or_1 (or_1_out, and_1_out, and_2_out);
  or or_2 (or_2_out, control_1_is_j1, control_1_is_j2);
  Register #(.width(32)) register_1 (
    .D(multiplexer_2_out), .en(1'b1), .clk(clock_1_out), .Q(register_1_q));  // open: clr
  Clock clock_1 (.out(clock_1_out));
  and and_1 (and_1_out, ~alu_1_regs_equal, control_1_is_bne);  // AND_Gate
  and and_2 (and_2_out, alu_1_regs_equal, control_1_is_beq);
  Shifter #(.shift("lr"), .width(32)) shifter_3 (.in(register_1_q), .\dist (5'b00010), .out(shifter_3_out));
  Bit_Extender #(.in_width(32)) bit_extender_3 (.in(shifter_3_out), .out(bit_extender_3_out));
  ROM #(.addrWidth(16), .dataWidth(32)) rom_1 (.addr(bit_extender_3_out), .data(rom_1_data));
  and and_3 (and_3_out, control_1_is_j3, control_1_is_j1);
  Multiplexer #(.width(32)) multiplexer_4 (
    .in0(multiplexer_6_out), .in1(adder_1_out), .out(multiplexer_4_out), .sel(control_1_is_j3));
  Multiplexer #(.width(5)) multiplexer_5 (
    .in0(control_1_rd), .in1({5{1'b1}}), .out(multiplexer_5_out), .sel(and_3_out));
  regfile regfile_1 (
    .rs_select(control_1_rs), .rt_select(control_1_rt), .rd_data(multiplexer_4_out),
    .rd_select(multiplexer_5_out), .write_enable(control_1_reg_write_e), .rs_data(regfile_1_rs_data),
    .rt_data(DataToBus));
  Control control_1 (
    .Inst(rom_1_data), .is_j3(control_1_is_j3), .is_j2(control_1_is_j2), .is_j1(control_1_is_j1),
    .is_beq(control_1_is_beq), .is_sw(BusWriteEnable), .is_lw(control_1_is_lw), .is_bne(control_1_is_bne),
    .rs(control_1_rs), .rt(control_1_rt), .rd(control_1_rd), .imm(control_1_imm),
    .reg_write_e(control_1_reg_write_e), .imm_sel(control_1_imm_sel), .ALU_code(control_1_alu_code));
  Multiplexer #(.width(32)) multiplexer_6 (
    .in0(alu_1_res), .in1(DataFromBus), .out(multiplexer_6_out), .sel(control_1_is_lw));
  Multiplexer #(.width(32)) multiplexer_7 (
    .in0(DataToBus), .in1(control_1_imm), .out(multiplexer_7_out), .sel(control_1_imm_sel));
  ALU alu_1 (
    .OP1(regfile_1_rs_data), .OP2(multiplexer_7_out), .ALU_CODE(control_1_alu_code), .Res(alu_1_res),
    .regs_equal(alu_1_regs_equal));
  Bit_Extender #(.in_width(32), .out_width(26)) bit_extender_4 (.in(alu_1_res), .out(AddressToBus));

  // Notes on the sheet:
  //   offset
  //   PC + 4
  //   offset + (PC + 4)
  //   j1 or j2
  //   contents of rom_1 (hex, n*v repeats v):
  //   1040001d 201b0001 105b001f 201b0004 105b0076 201b0005 105b003e 201b0008 105b007c 201b0009 105b005b
  //   201b000a 105b0062 201b000b 105b0061 201b000c 105b0061 201b000d 105b009e 201b000e 105b009e 201b000f
  //   105b009e 201b0010 105b009e 201b0011 105b009e 201b0012 105b00a2 800006f 23bdf000 201b0000 ac1bf100
  //   80000c3 23bdffe8 afa80000 afa90004 afaa0008 afab000c afac0010 afad0014 20880000 200d000a 20090000
  //   10d001a 23bdfffc 21290004 5010 afaa0000 4012 10d502a 1140fff8 21080030 ac08ff00 8fa80000 21080030
  //   ac08ff00 2129fffc 23bd0004 11200001 8000036 8fa80000 8fa90004 8faa0008 8fab000c 8fac0010 8fad0014
  //   23bd0018 3400008 23bdffe8 afa80000 afa90004 afaa0008 afab000c afac0010 afad0014 200a0000 200b000a
  //   200c002f 200d003a 8c08ff10 1100fffe 8c08ff14 188482a 11200008 10d482a 11200006 2108ffd0 14b0018 5012
  //   1485020 ac00ff10 8000050 21420000 8fa80000 8fa90004 8faa0008 8fab000c 8fac0010 8fad0014 23bd0018
  //   3400008 23bdfffc afa80000 8c08f100 21020000 1044020 ac08f100 8fa80000 23bd0004 3400008 800006f
  //   ac04ff00 3400008 23bdfffc afa80000 8c08ff10 1100fffe 8c02ff14 ac00ff10 8fa80000 23bd0004 3400008
  //   23bdfffc afa80000 8c880000 11000003 ac08ff00 20840004 800007d 8fa80000 23bd0004 3400008 23bdffe8
  //   afa80000 afa90004 afaa0008 afab000c afac0010 afa40014 200a000a 8c08ff10 1100fffe 8c09ff14 ac00ff10
  //   112a0004 23bdfffc 216b0004 afa90000 800008d 23bdfffc afba0000 1602020 20020009 d00c 8fba0000
  //   23bd0004 404020 10b4020 200a0000 ad0a0000 2108fffc 8fa90000 ad090000 23bd0004 216bfffc 116a0001
  //   80000a1 8fa80000 8fa90004 8faa0008 8fab000c 8fac0010 8fa40014 23bd0018 1001020 3400008 ac04ff30
  //   3400008 ac00ff34 3400008 8c02ff38 3400008 ac04ff3c 3400008 ac04ff40 ac05ff44 ac06ff48 ac07ff4c
  //   ac00ff58 3400008 8c02ff50 10400001 ac00ff54 3400008 20080032 84200 21040032 20050019 2006000a
  //   200700ff 20020011 d00c 20020012 d00c 14400002 21290001 80000cb 20080032 84200 21040096 2005000f
  //   20060028 200800ff 83c00 20020011 d00c 20020012 d00c 1440fff4 21290001 80000de 2002000a d00c
endmodule

module MemoryController (
  input  WriteEnableFromBus,
  input  [25:0] AddressFromBus,
  input  [31:0] DataFromBus,
  input  [31:0] DataFromMem,
  output [31:0] DataToBus,
  output WriteToBus,
  output WriteEnableToMem,
  output [23:0] AddressToMem,
  output [31:0] DataToMem
);

  wire comparator_1_lt;
  wire [25:0] shifter_1_out;

  Comparator #(.mode("unsigned"), .width(26)) comparator_1 (
    .a(AddressFromBus), .b(26'h3ffff00), .lt(comparator_1_lt));  // open: gt, eq
  and and_1 (WriteEnableToMem, WriteEnableFromBus, comparator_1_lt);
  and and_2 (WriteToBus, ~WriteEnableFromBus, comparator_1_lt);  // AND_Gate
  assign DataToBus = WriteToBus ? DataFromMem : 32'bz;  // Controlled_Buffer controlled_buffer_1
  Shifter #(.shift("lr"), .width(26)) shifter_1 (.in(AddressFromBus), .\dist (5'b00010), .out(shifter_1_out));
  assign DataToMem = WriteEnableToMem ? DataFromBus : 32'bz;  // Controlled_Buffer controlled_buffer_2
  Bit_Extender #(.in_width(26), .out_width(24)) bit_extender_1 (.in(shifter_1_out), .out(AddressToMem));
endmodule

module KeyboardController (
  input  [31:0] DataFromBus,
  input  WriteEnableFromBus,
  input  [25:0] AddressFromBus,
  input  [6:0] KeyboardData,
  input  KeyboardStatus,
  output WriteToBus,
  output [31:0] DataToBus,
  output KeyboardRead
);

  wire and_1_out, and_2_out, and_3_out, comparator_1_eq, comparator_2_eq;
  wire [31:0] bit_extender_1_out, bit_extender_2_out, controlled_buffer_1_out;

  Comparator #(.mode("unsigned"), .width(26)) comparator_1 (
    .a(AddressFromBus), .b(26'h3ffff10), .eq(comparator_1_eq));  // open: gt, lt
  Comparator #(.mode("unsigned"), .width(26)) comparator_2 (
    .a(AddressFromBus), .b(26'h3ffff14), .eq(comparator_2_eq));  // open: gt, lt
  and and_1 (and_1_out, WriteEnableFromBus, comparator_1_eq);
  and and_2 (and_2_out, ~WriteEnableFromBus, comparator_1_eq);  // AND_Gate
  and and_3 (and_3_out, ~WriteEnableFromBus, comparator_2_eq);  // AND_Gate
  assign bit_extender_1_out = {{25{1'b0}}, KeyboardData};  // Bit_Extender bit_extender_1
  assign bit_extender_2_out = {{31{1'b0}}, KeyboardStatus};  // Bit_Extender bit_extender_2
  or or_1 (WriteToBus, and_2_out, and_3_out);
  assign controlled_buffer_1_out = and_2_out ? bit_extender_2_out : 32'bz;  // Controlled_Buffer controlled_buffer_1
  Multiplexer #(.width(32)) multiplexer_1 (
    .in0(controlled_buffer_1_out), .in1(bit_extender_1_out), .out(DataToBus), .sel(and_3_out));
  Multiplexer multiplexer_2 (.in0(1'b0), .in1(KeyboardStatus), .out(KeyboardRead), .sel(and_1_out));
endmodule

module RGBController (
  input  [25:0] AddressFromBus,
  input  [31:0] DataFromBus,
  input  WriteEnable,
  output [7:0] RGBX,
  output [7:0] RGBY,
  output [23:0] RGBColor,
  output RGBWrite,
  output [31:0] data_tobus,
  output bus_we
);

  wire and_1_out, and_2_out, and_3_out, and_4_out, and_5_out, and_6_out, and_7_out, and_8_out, clock_1_out,
       clock_2_out, clock_3_out, clock_4_out, clock_5_out, clock_6_out, clock_7_out, clock_8_out,
       clock_9_out, clock_10_out, clock_11_out, comparator_1_eq, comparator_2_eq, comparator_3_eq,
       comparator_4_eq, comparator_5_eq, comparator_6_eq, comparator_7_eq, comparator_8_eq, comparator_10_eq,
       comparator_11_eq, comparator_12_eq, comparator_12_lt, comparator_13_eq, comparator_14_lt,
       multiplexer_8_out, not_1_out, or_1_out, or_2_out, register_9_q;
  wire [7:0] adder_1_out, adder_2_out, adder_3_out, adder_4_out, bit_extender_1_out, bit_extender_2_out,
       bit_extender_4_out, bit_extender_5_out, multiplexer_1_out, multiplexer_2_out, multiplexer_3_out,
       multiplexer_4_out, register_1_q, register_2_q, register_4_q, register_5_q, register_6_q, register_7_q,
       register_10_q, register_11_q;
  wire [23:0] bit_extender_3_out, bit_extender_6_out, register_3_q, register_8_q;
  wire [31:0] bit_extender_7_out;

  Comparator #(.mode("unsigned"), .width(26)) comparator_1 (
    .a(AddressFromBus), .b(26'h3ffff20), .eq(comparator_1_eq));  // open: gt, lt
  Comparator #(.mode("unsigned"), .width(26)) comparator_2 (
    .a(AddressFromBus), .b(26'h3ffff24), .eq(comparator_2_eq));  // open: gt, lt
  Comparator #(.mode("unsigned"), .width(26)) comparator_3 (
    .a(AddressFromBus), .b(26'h3ffff28), .eq(comparator_3_eq));  // open: gt, lt
  Comparator #(.mode("unsigned"), .width(26)) comparator_4 (
    .a(AddressFromBus), .b(26'h3ffff2c), .eq(comparator_4_eq));  // open: gt, lt
  Comparator #(.mode("unsigned"), .width(26)) comparator_5 (
    .a(AddressFromBus), .b(26'h3ffff40), .eq(comparator_5_eq));  // open: gt, lt
  Comparator #(.mode("unsigned"), .width(26)) comparator_6 (
    .a(AddressFromBus), .b(26'h3ffff44), .eq(comparator_6_eq));  // open: gt, lt
  Comparator #(.mode("unsigned"), .width(26)) comparator_7 (
    .a(AddressFromBus), .b(26'h3ffff48), .eq(comparator_7_eq));  // open: gt, lt
  Comparator #(.mode("unsigned"), .width(26)) comparator_8 (
    .a(AddressFromBus), .b(26'h3ffff4c), .eq(comparator_8_eq));  // open: gt, lt
  and and_1 (and_1_out, comparator_5_eq, WriteEnable);
  and and_2 (and_2_out, comparator_6_eq, WriteEnable);
  and and_3 (and_3_out, comparator_7_eq, WriteEnable);
  and and_4 (and_4_out, comparator_8_eq, WriteEnable);
  Comparator #(.mode("unsigned"), .width(26)) comparator_9 (
    .a(AddressFromBus), .b(26'h3ffff50), .eq(bus_we));  // open: gt, lt
  Comparator #(.mode("unsigned"), .width(26)) comparator_10 (
    .a(AddressFromBus), .b(26'h3ffff54), .eq(comparator_10_eq));  // open: gt, lt
  Comparator #(.mode("unsigned"), .width(26)) comparator_11 (
    .a(AddressFromBus), .b(26'h3ffff58), .eq(comparator_11_eq));  // open: gt, lt
  and and_5 (and_5_out, WriteEnable, comparator_1_eq);
  and and_6 (and_6_out, WriteEnable, comparator_2_eq);
  and and_7 (and_7_out, WriteEnable, comparator_3_eq);
  and and_8 (and_8_out, WriteEnable, comparator_4_eq);
  or or_1 (or_1_out, comparator_8_eq, comparator_7_eq, comparator_6_eq, comparator_5_eq);
  Register register_1 (.D(bit_extender_1_out), .en(and_5_out), .clk(clock_1_out), .Q(register_1_q));  // open: clr
  Bit_Extender #(.in_width(32), .out_width(8)) bit_extender_1 (.in(DataFromBus), .out(bit_extender_1_out));
  Clock clock_1 (.out(clock_1_out));
  Register register_2 (.D(bit_extender_2_out), .en(and_6_out), .clk(clock_2_out), .Q(register_2_q));  // open: clr
  Bit_Extender #(.in_width(32), .out_width(8)) bit_extender_2 (.in(DataFromBus), .out(bit_extender_2_out));
  Clock clock_2 (.out(clock_2_out));
  Register #(.width(24)) register_3 (
    .D(bit_extender_3_out), .en(and_7_out), .clk(clock_3_out), .Q(register_3_q));  // open: clr
  Bit_Extender #(.in_width(32), .out_width(24)) bit_extender_3 (.in(DataFromBus), .out(bit_extender_3_out));
  Clock clock_3 (.out(clock_3_out));
  Bit_Extender #(.in_width(32), .out_width(8)) bit_extender_4 (.in(DataFromBus), .out(bit_extender_4_out));
  Bit_Extender #(.in_width(32), .out_width(8)) bit_extender_5 (.in(DataFromBus), .out(bit_extender_5_out));
  Bit_Extender #(.in_width(32), .out_width(24)) bit_extender_6 (.in(DataFromBus), .out(bit_extender_6_out));
  Register register_4 (
    .D(DataFromBus[7:0]), .en(and_1_out), .clk(clock_4_out), .Q(register_4_q), .clr(comparator_10_eq));
  Clock clock_4 (.out(clock_4_out));
  Register register_5 (
    .D(DataFromBus[15:8]), .en(and_1_out), .clk(clock_5_out), .Q(register_5_q), .clr(comparator_10_eq));
  Clock clock_5 (.out(clock_5_out));
  Register register_6 (
    .D(bit_extender_4_out), .en(and_2_out), .clk(clock_6_out), .Q(register_6_q), .clr(comparator_10_eq));
  Clock clock_6 (.out(clock_6_out));
  Register register_7 (
    .D(bit_extender_5_out), .en(and_3_out), .clk(clock_7_out), .Q(register_7_q), .clr(comparator_10_eq));
  Clock clock_7 (.out(clock_7_out));
  Register #(.width(24)) register_8 (
    .D(bit_extender_6_out), .en(and_4_out), .clk(clock_8_out), .Q(register_8_q), .clr(comparator_10_eq));
  Clock clock_8 (.out(clock_8_out));
  Register #(.width(1)) register_9 (
    .D(or_1_out), .en(or_1_out), .clk(clock_9_out), .Q(register_9_q), .clr(comparator_13_eq));
  Clock clock_9 (.out(clock_9_out));
  Register register_10 (
    .D(multiplexer_2_out), .en(1'b1), .clk(clock_10_out), .Q(register_10_q), .clr(comparator_10_eq));
  Clock clock_10 (.out(clock_10_out));
  Multiplexer #(.width(8)) multiplexer_1 (
    .in0(adder_4_out), .in1(register_5_q), .out(multiplexer_1_out), .sel(comparator_11_eq));
  Multiplexer #(.width(8)) multiplexer_2 (
    .in0(adder_3_out), .in1(register_4_q), .out(multiplexer_2_out), .sel(comparator_12_eq));
  Register register_11 (
    .D(multiplexer_1_out), .en(1'b1), .clk(clock_11_out), .Q(register_11_q), .clr(comparator_10_eq));
  Clock clock_11 (.out(clock_11_out));
  Adder adder_1 (.a(register_4_q), .b(register_6_q), .out(adder_1_out));  // open: cin, cout
  Adder adder_2 (.a(register_5_q), .b(register_7_q), .out(adder_2_out));  // open: cin, cout
  Comparator #(.mode("unsigned")) comparator_12 (
    .a(register_10_q), .b(adder_1_out), .eq(comparator_12_eq), .lt(comparator_12_lt));  // open: gt
  Comparator #(.mode("unsigned")) comparator_13 (
    .a(register_11_q), .b(adder_2_out), .eq(comparator_13_eq));  // open: gt, lt
  Multiplexer #(.width(8)) multiplexer_3 (.in0({8{1'b0}}), .in1(8'h1), .out(multiplexer_3_out), .sel(comparator_12_lt));
  Multiplexer #(.width(8)) multiplexer_4 (.in0({8{1'b0}}), .in1(8'h1), .out(multiplexer_4_out), .sel(comparator_12_eq));
  Adder adder_3 (.a(register_10_q), .b(multiplexer_3_out), .out(adder_3_out));  // open: cin, cout
  Adder adder_4 (.a(register_11_q), .b(multiplexer_4_out), .out(adder_4_out));  // open: cin, cout
  or or_2 (or_2_out, comparator_13_eq, ~register_9_q);  // OR_Gate
  Multiplexer #(.width(8)) multiplexer_5 (.in0(register_1_q), .in1(register_10_q), .out(RGBX), .sel(register_9_q));
  Multiplexer #(.width(8)) multiplexer_6 (.in0(register_2_q), .in1(register_11_q), .out(RGBY), .sel(register_9_q));
  Multiplexer #(.width(24)) multiplexer_7 (.in0(register_3_q), .in1(register_8_q), .out(RGBColor), .sel(register_9_q));
  not not_1 (not_1_out, comparator_13_eq);
  Comparator #(.mode("unsigned")) comparator_14 (
    .a(register_10_q), .b(register_4_q), .lt(comparator_14_lt));  // open: gt, eq
  assign bit_extender_7_out = {{31{1'b0}}, or_2_out};  // Bit_Extender bit_extender_7
  assign data_tobus = bus_we ? bit_extender_7_out : 32'bz;  // Controlled_Buffer controlled_buffer_1
  Multiplexer multiplexer_8 (.in0(not_1_out), .in1(1'b0), .out(multiplexer_8_out), .sel(comparator_14_lt));
  Multiplexer multiplexer_9 (.in0(and_8_out), .in1(multiplexer_8_out), .out(RGBWrite), .sel(register_9_q));
endmodule

module TerminalController (
  input  WriteEnableFromBus,
  input  [25:0] AddressFromBus,
  input  [31:0] DataFromBus,
  output [6:0] DataToTerminal,
  output WriteToTerminal
);

  wire comparator_1_eq;
  wire [31:0] controlled_buffer_1_out;

  Comparator #(.mode("unsigned"), .width(26)) comparator_1 (
    .a(AddressFromBus), .b(26'h3ffff00), .eq(comparator_1_eq));  // open: gt, lt
  and and_1 (WriteToTerminal, WriteEnableFromBus, comparator_1_eq);
  assign controlled_buffer_1_out = WriteToTerminal ? DataFromBus : 32'bz;  // Controlled_Buffer controlled_buffer_1
  Bit_Extender #(.in_width(32), .out_width(7)) bit_extender_1 (.in(controlled_buffer_1_out), .out(DataToTerminal));
endmodule

module CPUmain (
);

  wire alu_1_regs_equal, and_1_out, and_2_out, clock_1_out, clock_2_out, control_1_imm_sel, control_1_is_beq,
       control_1_is_bne, control_1_is_j1, control_1_is_j2, control_1_is_j3, control_1_is_lw, control_1_is_sw,
       control_1_reg_write_e, or_1_out, or_2_out;
  wire [3:0] control_1_alu_code;
  wire [4:0] control_1_rd, control_1_rs, control_1_rt, multiplexer_5_out;
  wire [15:0] bit_extender_3_out, bit_extender_4_out;
  wire [25:0] bit_extender_1_out;
  wire [31:0] adder_1_out, adder_2_out, alu_1_res, bit_extender_2_out, control_1_imm, multiplexer_1_out,
       multiplexer_2_out, multiplexer_3_out, multiplexer_4_out, multiplexer_6_out, multiplexer_7_out,
       ram_1_dout, regfile_1_rs_data, regfile_1_rt_data, register_1_q, rom_1_data, shifter_1_out,
       shifter_2_out, shifter_3_out, shifter_4_out;

  Adder #(.width(32)) adder_1 (.a(register_1_q), .b(32'h4), .out(adder_1_out));  // open: cin, cout
  Shifter #(.width(32)) shifter_1 (.in(control_1_imm), .\dist (5'b00010), .out(shifter_1_out));
  Adder #(.width(32)) adder_2 (.a(adder_1_out), .b(shifter_1_out), .out(adder_2_out));  // open: cin, cout
  Bit_Extender #(.in_width(32), .out_width(26), .\type ("zero")) bit_extender_1 (
    .in(rom_1_data), .out(bit_extender_1_out));
  assign bit_extender_2_out = {{6{1'b0}}, bit_extender_1_out};  // Bit_Extender bit_extender_2
  Multiplexer #(.width(32)) multiplexer_1 (
    .in0(adder_1_out), .in1(adder_2_out), .out(multiplexer_1_out), .sel(or_1_out));
  Shifter #(.width(32)) shifter_2 (.in(bit_extender_2_out), .\dist (5'b00010), .out(shifter_2_out));
  Multiplexer #(.width(32)) multiplexer_2 (
    .in0(multiplexer_1_out), .in1(multiplexer_3_out), .out(multiplexer_2_out), .sel(or_2_out));
  Multiplexer #(.width(32)) multiplexer_3 (
    .in0(regfile_1_rs_data), .in1(shifter_2_out), .out(multiplexer_3_out), .sel(control_1_is_j1));
  or or_1 (or_1_out, and_1_out, and_2_out);
  or or_2 (or_2_out, control_1_is_j1, control_1_is_j2);
  Register #(.width(32)) register_1 (
    .D(multiplexer_2_out), .en(1'b1), .clk(clock_1_out), .Q(register_1_q));  // open: clr
  Clock clock_1 (.out(clock_1_out));
  and and_1 (and_1_out, ~alu_1_regs_equal, control_1_is_bne);  // AND_Gate
  and and_2 (and_2_out, alu_1_regs_equal, control_1_is_beq);
  Shifter #(.shift("lr"), .width(32)) shifter_3 (.in(register_1_q), .\dist (5'b00010), .out(shifter_3_out));
  Bit_Extender #(.in_width(32)) bit_extender_3 (.in(shifter_3_out), .out(bit_extender_3_out));
  ROM #(.addrWidth(16), .dataWidth(32)) rom_1 (.addr(bit_extender_3_out), .data(rom_1_data));
  Multiplexer #(.width(32)) multiplexer_4 (
    .in0(multiplexer_6_out), .in1(adder_1_out), .out(multiplexer_4_out), .sel(control_1_is_j3));
  Multiplexer #(.width(5)) multiplexer_5 (
    .in0(control_1_rd), .in1({5{1'b1}}), .out(multiplexer_5_out), .sel(control_1_is_j3));
  regfile regfile_1 (
    .rs_select(control_1_rs), .rt_select(control_1_rt), .rd_data(multiplexer_4_out),
    .rd_select(multiplexer_5_out), .write_enable(control_1_reg_write_e), .rs_data(regfile_1_rs_data),
    .rt_data(regfile_1_rt_data));
  Control control_1 (
    .Inst(rom_1_data), .is_j3(control_1_is_j3), .is_j2(control_1_is_j2), .is_j1(control_1_is_j1),
    .is_beq(control_1_is_beq), .is_sw(control_1_is_sw), .is_lw(control_1_is_lw), .is_bne(control_1_is_bne),
    .rs(control_1_rs), .rt(control_1_rt), .rd(control_1_rd), .imm(control_1_imm),
    .reg_write_e(control_1_reg_write_e), .imm_sel(control_1_imm_sel), .ALU_code(control_1_alu_code));
  Multiplexer #(.width(32)) multiplexer_6 (
    .in0(alu_1_res), .in1(ram_1_dout), .out(multiplexer_6_out), .sel(control_1_is_lw));
  Multiplexer #(.width(32)) multiplexer_7 (
    .in0(regfile_1_rt_data), .in1(control_1_imm), .out(multiplexer_7_out), .sel(control_1_imm_sel));
  ALU alu_1 (
    .OP1(regfile_1_rs_data), .OP2(multiplexer_7_out), .ALU_CODE(control_1_alu_code), .Res(alu_1_res),
    .regs_equal(alu_1_regs_equal));
  Shifter #(.shift("lr"), .width(32)) shifter_4 (.in(alu_1_res), .\dist (5'b00010), .out(shifter_4_out));
  RAM #(.addrWidth(16), .dataWidth(32), .enables("line")) ram_1 (
    .addr(bit_extender_4_out), .we(control_1_is_sw), .clk(clock_2_out), .din(regfile_1_rt_data),
    .dout(ram_1_dout));
  Bit_Extender #(.in_width(32)) bit_extender_4 (.in(shifter_4_out), .out(bit_extender_4_out));
  Clock clock_2 (.out(clock_2_out));

  // Notes on the sheet:
  //   offset
  //   PC + 4
  //   offset + (PC + 4)
  //   j1 or j2
endmodule

module regfile (
  input  write_enable,
  input  [4:0] rd_select,
  input  [31:0] rd_data,
  input  [4:0] rs_select,
  input  [4:0] rt_select,
  output [31:0] rs_data,
  output [31:0] rt_data
);

  wire and_1_out, clock_1_out, clock_2_out, clock_3_out, clock_4_out, clock_5_out, clock_6_out, clock_7_out,
       clock_8_out, clock_9_out, clock_10_out, clock_11_out, clock_12_out, clock_13_out, clock_14_out,
       clock_15_out, clock_16_out, clock_17_out, clock_18_out, clock_19_out, clock_20_out, clock_21_out,
       clock_22_out, clock_23_out, clock_24_out, clock_25_out, clock_26_out, clock_27_out, clock_28_out,
       clock_29_out, clock_30_out, clock_31_out, comparator_1_eq, comparator_2_gt, comparator_3_gt,
       demultiplexer_2_out1, demultiplexer_2_out2, demultiplexer_2_out3, demultiplexer_2_out4,
       demultiplexer_2_out5, demultiplexer_2_out6, demultiplexer_2_out7, demultiplexer_2_out8,
       demultiplexer_2_out9, demultiplexer_2_out10, demultiplexer_2_out11, demultiplexer_2_out12,
       demultiplexer_2_out13, demultiplexer_2_out14, demultiplexer_2_out15, demultiplexer_2_out16,
       demultiplexer_2_out17, demultiplexer_2_out18, demultiplexer_2_out19, demultiplexer_2_out20,
       demultiplexer_2_out21, demultiplexer_2_out22, demultiplexer_2_out23, demultiplexer_2_out24,
       demultiplexer_2_out25, demultiplexer_2_out26, demultiplexer_2_out27, demultiplexer_2_out28,
       demultiplexer_2_out29, demultiplexer_2_out30, demultiplexer_2_out31;
  wire [31:0] demultiplexer_1_out1, demultiplexer_1_out2, demultiplexer_1_out3, demultiplexer_1_out4,
       demultiplexer_1_out5, demultiplexer_1_out6, demultiplexer_1_out7, demultiplexer_1_out8,
       demultiplexer_1_out9, demultiplexer_1_out10, demultiplexer_1_out11, demultiplexer_1_out12,
       demultiplexer_1_out13, demultiplexer_1_out14, demultiplexer_1_out15, demultiplexer_1_out16,
       demultiplexer_1_out17, demultiplexer_1_out18, demultiplexer_1_out19, demultiplexer_1_out20,
       demultiplexer_1_out21, demultiplexer_1_out22, demultiplexer_1_out23, demultiplexer_1_out24,
       demultiplexer_1_out25, demultiplexer_1_out26, demultiplexer_1_out27, demultiplexer_1_out28,
       demultiplexer_1_out29, demultiplexer_1_out30, demultiplexer_1_out31, multiplexer_1_out,
       multiplexer_2_out, register_1_q, register_2_q, register_3_q, register_4_q, register_5_q, register_6_q,
       register_7_q, register_8_q, register_9_q, register_10_q, register_11_q, register_12_q, register_13_q,
       register_14_q, register_15_q, register_16_q, register_17_q, register_18_q, register_19_q,
       register_20_q, register_21_q, register_22_q, register_23_q, register_24_q, register_25_q,
       register_26_q, register_27_q, register_28_q, register_29_q, register_30_q, register_31_q;

  Demultiplexer #(.select(5), .width(32)) demultiplexer_1 (
    .out1(demultiplexer_1_out1), .out2(demultiplexer_1_out2), .out3(demultiplexer_1_out3),
    .out4(demultiplexer_1_out4), .out5(demultiplexer_1_out5), .out6(demultiplexer_1_out6),
    .out7(demultiplexer_1_out7), .out8(demultiplexer_1_out8), .out9(demultiplexer_1_out9),
    .out10(demultiplexer_1_out10), .out11(demultiplexer_1_out11), .out12(demultiplexer_1_out12),
    .out13(demultiplexer_1_out13), .out14(demultiplexer_1_out14), .out15(demultiplexer_1_out15),
    .out16(demultiplexer_1_out16), .out17(demultiplexer_1_out17), .out18(demultiplexer_1_out18),
    .out19(demultiplexer_1_out19), .out20(demultiplexer_1_out20), .out21(demultiplexer_1_out21),
    .out22(demultiplexer_1_out22), .out23(demultiplexer_1_out23), .out24(demultiplexer_1_out24),
    .out25(demultiplexer_1_out25), .out26(demultiplexer_1_out26), .out27(demultiplexer_1_out27),
    .out28(demultiplexer_1_out28), .out29(demultiplexer_1_out29), .out30(demultiplexer_1_out30),
    .out31(demultiplexer_1_out31), .in(rd_data), .sel(rd_select));  // open: out0
  Comparator #(.mode("unsigned"), .width(5)) comparator_1 (
    .a({5{1'b0}}), .b(rd_select), .eq(comparator_1_eq));  // open: gt, lt
  and and_1 (and_1_out, write_enable, ~comparator_1_eq);  // AND_Gate
  Demultiplexer #(.select(5)) demultiplexer_2 (
    .out1(demultiplexer_2_out1), .out2(demultiplexer_2_out2), .out3(demultiplexer_2_out3),
    .out4(demultiplexer_2_out4), .out5(demultiplexer_2_out5), .out6(demultiplexer_2_out6),
    .out7(demultiplexer_2_out7), .out8(demultiplexer_2_out8), .out9(demultiplexer_2_out9),
    .out10(demultiplexer_2_out10), .out11(demultiplexer_2_out11), .out12(demultiplexer_2_out12),
    .out13(demultiplexer_2_out13), .out14(demultiplexer_2_out14), .out15(demultiplexer_2_out15),
    .out16(demultiplexer_2_out16), .out17(demultiplexer_2_out17), .out18(demultiplexer_2_out18),
    .out19(demultiplexer_2_out19), .out20(demultiplexer_2_out20), .out21(demultiplexer_2_out21),
    .out22(demultiplexer_2_out22), .out23(demultiplexer_2_out23), .out24(demultiplexer_2_out24),
    .out25(demultiplexer_2_out25), .out26(demultiplexer_2_out26), .out27(demultiplexer_2_out27),
    .out28(demultiplexer_2_out28), .out29(demultiplexer_2_out29), .out30(demultiplexer_2_out30),
    .out31(demultiplexer_2_out31), .in(and_1_out), .sel(rd_select));  // open: out0
  Register #(.width(32)) register_1 (
    .D(demultiplexer_1_out1), .en(demultiplexer_2_out1), .clk(clock_1_out), .Q(register_1_q));  // open: clr
  Clock clock_1 (.out(clock_1_out));
  Register #(.width(32)) register_2 (
    .D(demultiplexer_1_out2), .en(demultiplexer_2_out2), .clk(clock_2_out), .Q(register_2_q));  // open: clr
  Clock clock_2 (.out(clock_2_out));
  Register #(.width(32)) register_3 (
    .D(demultiplexer_1_out3), .en(demultiplexer_2_out3), .clk(clock_3_out), .Q(register_3_q));  // open: clr
  Clock clock_3 (.out(clock_3_out));
  Register #(.width(32)) register_4 (
    .D(demultiplexer_1_out4), .en(demultiplexer_2_out4), .clk(clock_4_out), .Q(register_4_q));  // open: clr
  Clock clock_4 (.out(clock_4_out));
  Register #(.width(32)) register_5 (
    .D(demultiplexer_1_out5), .en(demultiplexer_2_out5), .clk(clock_5_out), .Q(register_5_q));  // open: clr
  Clock clock_5 (.out(clock_5_out));
  Register #(.width(32)) register_6 (
    .D(demultiplexer_1_out6), .en(demultiplexer_2_out6), .clk(clock_6_out), .Q(register_6_q));  // open: clr
  Clock clock_6 (.out(clock_6_out));
  Register #(.width(32)) register_7 (
    .D(demultiplexer_1_out7), .en(demultiplexer_2_out7), .clk(clock_7_out), .Q(register_7_q));  // open: clr
  Clock clock_7 (.out(clock_7_out));
  Register #(.width(32)) register_8 (
    .D(demultiplexer_1_out8), .en(demultiplexer_2_out8), .clk(clock_8_out), .Q(register_8_q));  // open: clr
  Clock clock_8 (.out(clock_8_out));
  Register #(.width(32)) register_9 (
    .D(demultiplexer_1_out9), .en(demultiplexer_2_out9), .clk(clock_9_out), .Q(register_9_q));  // open: clr
  Clock clock_9 (.out(clock_9_out));
  Register #(.width(32)) register_10 (
    .D(demultiplexer_1_out10), .en(demultiplexer_2_out10), .clk(clock_10_out), .Q(register_10_q));  // open: clr
  Clock clock_10 (.out(clock_10_out));
  Register #(.width(32)) register_11 (
    .D(demultiplexer_1_out11), .en(demultiplexer_2_out11), .clk(clock_11_out), .Q(register_11_q));  // open: clr
  Clock clock_11 (.out(clock_11_out));
  Register #(.width(32)) register_12 (
    .D(demultiplexer_1_out12), .en(demultiplexer_2_out12), .clk(clock_12_out), .Q(register_12_q));  // open: clr
  Clock clock_12 (.out(clock_12_out));
  Register #(.width(32)) register_13 (
    .D(demultiplexer_1_out13), .en(demultiplexer_2_out13), .clk(clock_13_out), .Q(register_13_q));  // open: clr
  Clock clock_13 (.out(clock_13_out));
  Register #(.width(32)) register_14 (
    .D(demultiplexer_1_out14), .en(demultiplexer_2_out14), .clk(clock_14_out), .Q(register_14_q));  // open: clr
  Clock clock_14 (.out(clock_14_out));
  Register #(.width(32)) register_15 (
    .D(demultiplexer_1_out15), .en(demultiplexer_2_out15), .clk(clock_15_out), .Q(register_15_q));  // open: clr
  Clock clock_15 (.out(clock_15_out));
  Register #(.width(32)) register_16 (
    .D(demultiplexer_1_out16), .en(demultiplexer_2_out16), .clk(clock_16_out), .Q(register_16_q));  // open: clr
  Clock clock_16 (.out(clock_16_out));
  Register #(.width(32)) register_17 (
    .D(demultiplexer_1_out17), .en(demultiplexer_2_out17), .clk(clock_17_out), .Q(register_17_q));  // open: clr
  Clock clock_17 (.out(clock_17_out));
  Register #(.width(32)) register_18 (
    .D(demultiplexer_1_out18), .en(demultiplexer_2_out18), .clk(clock_18_out), .Q(register_18_q));  // open: clr
  Clock clock_18 (.out(clock_18_out));
  Register #(.width(32)) register_19 (
    .D(demultiplexer_1_out19), .en(demultiplexer_2_out19), .clk(clock_19_out), .Q(register_19_q));  // open: clr
  Clock clock_19 (.out(clock_19_out));
  Register #(.width(32)) register_20 (
    .D(demultiplexer_1_out20), .en(demultiplexer_2_out20), .clk(clock_20_out), .Q(register_20_q));  // open: clr
  Clock clock_20 (.out(clock_20_out));
  Register #(.width(32)) register_21 (
    .D(demultiplexer_1_out21), .en(demultiplexer_2_out21), .clk(clock_21_out), .Q(register_21_q));  // open: clr
  Clock clock_21 (.out(clock_21_out));
  Register #(.width(32)) register_22 (
    .D(demultiplexer_1_out22), .en(demultiplexer_2_out22), .clk(clock_22_out), .Q(register_22_q));  // open: clr
  Clock clock_22 (.out(clock_22_out));
  Register #(.width(32)) register_23 (
    .D(demultiplexer_1_out23), .en(demultiplexer_2_out23), .clk(clock_23_out), .Q(register_23_q));  // open: clr
  Clock clock_23 (.out(clock_23_out));
  Register #(.width(32)) register_24 (
    .D(demultiplexer_1_out24), .en(demultiplexer_2_out24), .clk(clock_24_out), .Q(register_24_q));  // open: clr
  Clock clock_24 (.out(clock_24_out));
  Register #(.width(32)) register_25 (
    .D(demultiplexer_1_out25), .en(demultiplexer_2_out25), .clk(clock_25_out), .Q(register_25_q));  // open: clr
  Clock clock_25 (.out(clock_25_out));
  Register #(.width(32)) register_26 (
    .D(demultiplexer_1_out26), .en(demultiplexer_2_out26), .clk(clock_26_out), .Q(register_26_q));  // open: clr
  Clock clock_26 (.out(clock_26_out));
  Register #(.width(32)) register_27 (
    .D(demultiplexer_1_out27), .en(demultiplexer_2_out27), .clk(clock_27_out), .Q(register_27_q));  // open: clr
  Clock clock_27 (.out(clock_27_out));
  Register #(.width(32)) register_28 (
    .D(demultiplexer_1_out28), .en(demultiplexer_2_out28), .clk(clock_28_out), .Q(register_28_q));  // open: clr
  Clock clock_28 (.out(clock_28_out));
  Register #(.width(32)) register_29 (
    .D(demultiplexer_1_out29), .en(demultiplexer_2_out29), .clk(clock_29_out), .Q(register_29_q));  // open: clr
  Clock clock_29 (.out(clock_29_out));
  Register #(.width(32)) register_30 (
    .D(demultiplexer_1_out30), .en(demultiplexer_2_out30), .clk(clock_30_out), .Q(register_30_q));  // open: clr
  Clock clock_30 (.out(clock_30_out));
  Register #(.width(32)) register_31 (
    .D(demultiplexer_1_out31), .en(demultiplexer_2_out31), .clk(clock_31_out), .Q(register_31_q));  // open: clr
  Clock clock_31 (.out(clock_31_out));
  Multiplexer #(.select(5), .width(32)) multiplexer_1 (
    .in1(register_1_q), .in2(register_2_q), .in3(register_3_q), .in4(register_4_q), .in5(register_5_q),
    .in6(register_6_q), .in7(register_7_q), .in8(register_8_q), .in9(register_9_q), .in10(register_10_q),
    .in11(register_11_q), .in12(register_12_q), .in13(register_13_q), .in14(register_14_q),
    .in15(register_15_q), .in16(register_16_q), .in17(register_17_q), .in18(register_18_q),
    .in19(register_19_q), .in20(register_20_q), .in21(register_21_q), .in22(register_22_q),
    .in23(register_23_q), .in24(register_24_q), .in25(register_25_q), .in26(register_26_q),
    .in27(register_27_q), .in28(register_28_q), .in29(register_29_q), .in30(register_30_q),
    .in31(register_31_q), .out(multiplexer_1_out), .sel(rs_select));  // open: in0
  Comparator #(.mode("unsigned"), .width(5)) comparator_2 (
    .a(rs_select), .b({5{1'b0}}), .gt(comparator_2_gt));  // open: eq, lt
  Multiplexer #(.select(5), .width(32)) multiplexer_2 (
    .in1(register_1_q), .in2(register_2_q), .in3(register_3_q), .in4(register_4_q), .in5(register_5_q),
    .in6(register_6_q), .in7(register_7_q), .in8(register_8_q), .in9(register_9_q), .in10(register_10_q),
    .in11(register_11_q), .in12(register_12_q), .in13(register_13_q), .in14(register_14_q),
    .in15(register_15_q), .in16(register_16_q), .in17(register_17_q), .in18(register_18_q),
    .in19(register_19_q), .in20(register_20_q), .in21(register_21_q), .in22(register_22_q),
    .in23(register_23_q), .in24(register_24_q), .in25(register_25_q), .in26(register_26_q),
    .in27(register_27_q), .in28(register_28_q), .in29(register_29_q), .in30(register_30_q),
    .in31(register_31_q), .out(multiplexer_2_out), .sel(rt_select));  // open: in0
  Multiplexer #(.width(32)) multiplexer_3 (
    .in0({32{1'b0}}), .in1(multiplexer_1_out), .out(rs_data), .sel(comparator_2_gt));
  Comparator #(.mode("unsigned"), .width(5)) comparator_3 (
    .a(rt_select), .b({5{1'b0}}), .gt(comparator_3_gt));  // open: eq, lt
  Multiplexer #(.width(32)) multiplexer_4 (
    .in0({32{1'b0}}), .in1(multiplexer_2_out), .out(rt_data), .sel(comparator_3_gt));

  // Notes on the sheet:
  //   1, $at
  //   2, $v0
  //   3, $v1
  //   4, $a0
  //   5, $a1
  //   6, $a2
  //   7, $a3
  //   8, $t0
  //   9, $t1
  //   10, $t2
  //   11, $t3
  //   12, $t4
  //   13, $t5
  //   14, $t6
  //   15, $t7
  //   16, $s0
  //   17, $s1
  //   18, $s2
  //   19, $s3
  //   20, $s4
  //   21, $s5
  //   22, $s6
  //   23, $s7
  //   24, $t8
  //   25, $t9
  //   26, $k0
  //   27, $k1
  //   28, $gp
  //   29, $sp
  //   30, $fp
  //   31, $ra
endmodule

module ALU (
  input  [3:0] ALU_CODE,
  input  [31:0] OP1,
  input  [31:0] OP2,
  output [31:0] Res,
  output regs_equal
);

  wire clock_1_out, clock_2_out, comparator_1_lt, comparator_2_eq, comparator_3_eq, or_1_out;
  wire [4:0] bit_extender_1_out;
  wire [31:0] adder_1_out, bit_extender_2_out, divider_1_out, divider_1_rem, HI_q, LO_q, multiplexer_1_out,
       multiplexer_2_out, multiplier_1_cout, multiplier_1_out, shifter_1_out, shifter_2_out, subtractor_1_out;

  Bit_Extender #(.in_width(32), .out_width(5)) bit_extender_1 (.in(OP2), .out(bit_extender_1_out));
  Adder #(.width(32)) adder_1 (.a(OP1), .b(OP2), .out(adder_1_out));  // open: cin, cout
  Subtractor #(.width(32)) subtractor_1 (.a(OP1), .b(OP2), .out(subtractor_1_out));  // open: bin, bout
  Multiplier #(.mode("twosComplement"), .width(32)) multiplier_1 (
    .a(OP1), .b(OP2), .out(multiplier_1_out), .cout(multiplier_1_cout));  // open: cin
  Divider #(.mode("twosComplement"), .width(32)) divider_1 (
    .a(OP1), .b(OP2), .out(divider_1_out), .rem(divider_1_rem));  // open: upper
  Comparator #(.width(32)) comparator_1 (.a(OP1), .b(OP2), .eq(regs_equal), .lt(comparator_1_lt));  // open: gt
  Shifter #(.shift("lr"), .width(32)) shifter_1 (.in(OP1), .\dist (bit_extender_1_out), .out(shifter_1_out));
  Shifter #(.width(32)) shifter_2 (.in(OP1), .\dist (bit_extender_1_out), .out(shifter_2_out));
  Comparator #(.mode("unsigned"), .width(4)) comparator_2 (
    .a(4'b0010), .b(ALU_CODE), .eq(comparator_2_eq));  // open: gt, lt
  Comparator #(.mode("unsigned"), .width(4)) comparator_3 (
    .a(4'b0011), .b(ALU_CODE), .eq(comparator_3_eq));  // open: gt, lt
  Multiplexer #(.width(32)) multiplexer_1 (
    .in0(divider_1_rem), .in1(multiplier_1_cout), .out(multiplexer_1_out), .sel(comparator_2_eq));
  or or_1 (or_1_out, comparator_2_eq, comparator_3_eq);
  Multiplexer #(.width(32)) multiplexer_2 (
    .in0(multiplier_1_out), .in1(divider_1_out), .out(multiplexer_2_out), .sel(comparator_3_eq));
  Register #(.width(32)) HI (.D(multiplexer_1_out), .en(or_1_out), .clk(clock_1_out), .Q(HI_q));  // open: clr
  Clock clock_1 (.out(clock_1_out));
  Register #(.width(32)) LO (.D(multiplexer_2_out), .en(or_1_out), .clk(clock_2_out), .Q(LO_q));  // open: clr
  Clock clock_2 (.out(clock_2_out));
  assign bit_extender_2_out = {{31{1'b0}}, comparator_1_lt};  // Bit_Extender bit_extender_2
  Multiplexer #(.select(4), .width(32)) multiplexer_3 (
    .in0(adder_1_out), .in1(subtractor_1_out), .in4(shifter_2_out), .in5(shifter_1_out),
    .in6(bit_extender_2_out), .in7(HI_q), .in8(LO_q), .out(Res), .sel(ALU_CODE));  // open: in2, in3, in9, in10, in11, in12, in13, in14, in15
endmodule

module Control (
  input  [31:0] Inst,
  output is_j3,
  output is_j2,
  output is_j1,
  output is_beq,
  output is_sw,
  output is_lw,
  output is_bne,
  output [4:0] rs,
  output [4:0] rt,
  output [4:0] rd,
  output [31:0] imm,
  output reg_write_e,
  output imm_sel,
  output [3:0] ALU_code
);

  wire and_1_out, and_2_out, and_3_out, and_4_out, and_5_out, and_6_out, and_7_out, and_8_out,
       comparator_1_eq, comparator_2_eq, comparator_3_eq, comparator_7_eq, comparator_8_eq, comparator_9_eq,
       comparator_10_eq, comparator_11_eq, comparator_12_eq, comparator_13_eq, comparator_14_eq,
       comparator_15_eq, comparator_16_eq, comparator_17_eq, comparator_19_eq, comparator_20_eq,
       comparator_21_eq, comparator_22_eq, comparator_23_eq, comparator_24_eq, comparator_25_eq, or_1_out,
       or_2_out, or_3_out, or_4_out, or_7_out, or_9_out, or_10_out, or_12_out, or_13_out, or_15_out;
  wire [3:0] multiplexer_2_out, multiplexer_3_out, multiplexer_4_out, multiplexer_5_out, multiplexer_6_out,
       multiplexer_7_out, multiplexer_8_out, multiplexer_9_out, multiplexer_10_out, multiplexer_12_out,
       or_11_out;
  wire [4:0] multiplexer_11_out;
  wire [5:0] multiplexer_1_out;
  wire [31:0] bit_extender_1_out, bit_extender_2_out;

  or or_1 (or_1_out, is_beq, is_bne, and_6_out, is_sw, comparator_19_eq);
  Comparator #(.mode("unsigned"), .width(6)) comparator_1 (
    .a(6'b001100), .b(Inst[5:0]), .eq(comparator_1_eq));  // open: gt, lt
  or or_2 (or_2_out, is_beq, is_bne);
  and and_1 (and_1_out, and_2_out, ~comparator_3_eq);  // AND_Gate
  and and_2 (and_2_out, comparator_2_eq, comparator_1_eq);
  Comparator #(.mode("unsigned"), .width(6)) comparator_2 (
    .a({6{1'b0}}), .b(Inst[31:26]), .eq(comparator_2_eq));  // open: gt, lt
  Comparator #(.width(6)) comparator_3 (.a(6'b001000), .b(Inst[31:26]), .eq(comparator_3_eq));  // open: gt, lt
  Comparator #(.mode("unsigned"), .width(6)) comparator_4 (.a(6'b101011), .b(Inst[31:26]), .eq(is_sw));  // open: gt, lt
  Multiplexer #(.width(6)) multiplexer_1 (
    .in0(Inst[5:0]), .in1(6'b100000), .out(multiplexer_1_out), .sel(comparator_3_eq));
  Comparator #(.mode("unsigned"), .width(6)) comparator_5 (.a(6'b100011), .b(Inst[31:26]), .eq(is_lw));  // open: gt, lt
  Comparator #(.mode("unsigned"), .width(6)) comparator_6 (
    .a(6'b000101), .b(Inst[31:26]), .eq(is_bne));  // open: gt, lt
  Comparator #(.width(6)) comparator_7 (.a(6'b011000), .b(Inst[5:0]), .eq(comparator_7_eq));  // open: gt, lt
  Comparator #(.width(6)) comparator_8 (.a(6'b011010), .b(Inst[5:0]), .eq(comparator_8_eq));  // open: gt, lt
  Comparator #(.width(6)) comparator_9 (.a(6'b100000), .b(multiplexer_1_out), .eq(comparator_9_eq));  // open: gt, lt
  Comparator #(.width(6)) comparator_10 (.a(6'b100010), .b(multiplexer_1_out), .eq(comparator_10_eq));  // open: gt, lt
  Comparator #(.width(6)) comparator_11 (.a(6'b011000), .b(multiplexer_1_out), .eq(comparator_11_eq));  // open: gt, lt
  Comparator #(.width(6)) comparator_12 (.a(6'b011010), .b(multiplexer_1_out), .eq(comparator_12_eq));  // open: gt, lt
  Comparator #(.width(6)) comparator_13 (.a({6{1'b0}}), .b(multiplexer_1_out), .eq(comparator_13_eq));  // open: gt, lt
  Comparator #(.width(6)) comparator_14 (.a(6'b000010), .b(multiplexer_1_out), .eq(comparator_14_eq));  // open: gt, lt
  Comparator #(.width(6)) comparator_15 (.a(6'b101010), .b(multiplexer_1_out), .eq(comparator_15_eq));  // open: gt, lt
  Comparator #(.width(6)) comparator_16 (.a(6'b010000), .b(multiplexer_1_out), .eq(comparator_16_eq));  // open: gt, lt
  Comparator #(.width(6)) comparator_17 (.a(6'b010010), .b(multiplexer_1_out), .eq(comparator_17_eq));  // open: gt, lt
  or or_3 (or_3_out, is_sw, is_lw);
  Comparator #(.mode("unsigned"), .width(6)) comparator_18 (
    .a(6'b000100), .b(Inst[31:26]), .eq(is_beq));  // open: gt, lt
  Comparator #(.mode("unsigned"), .width(6)) comparator_19 (
    .a(6'b000010), .b(Inst[31:26]), .eq(comparator_19_eq));  // open: gt, lt
  or or_4 (or_4_out, comparator_7_eq, comparator_8_eq);
  or or_5 (is_j1, comparator_19_eq, comparator_21_eq);
  Comparator #(.width(6)) comparator_20 (.a(Inst[31:26]), .b({6{1'b0}}), .eq(comparator_20_eq));  // open: gt, lt
  Multiplexer #(.width(4)) multiplexer_2 (.in0(4'b0000), .in1(4'b0000), .out(multiplexer_2_out), .sel(comparator_9_eq));
  Multiplexer #(.width(4)) multiplexer_3 (
    .in0(4'b0000), .in1(4'b0001), .out(multiplexer_3_out), .sel(comparator_10_eq));
  Multiplexer #(.width(4)) multiplexer_4 (
    .in0(4'b0000), .in1(4'b0010), .out(multiplexer_4_out), .sel(comparator_11_eq));
  Multiplexer #(.width(4)) multiplexer_5 (
    .in0(4'b0000), .in1(4'b0011), .out(multiplexer_5_out), .sel(comparator_12_eq));
  Multiplexer #(.width(4)) multiplexer_6 (
    .in0(4'b0000), .in1(4'b0100), .out(multiplexer_6_out), .sel(comparator_13_eq));
  Multiplexer #(.width(4)) multiplexer_7 (
    .in0(4'b0000), .in1(4'b0101), .out(multiplexer_7_out), .sel(comparator_14_eq));
  Multiplexer #(.width(4)) multiplexer_8 (
    .in0(4'b0000), .in1(4'b0110), .out(multiplexer_8_out), .sel(comparator_15_eq));
  Multiplexer #(.width(4)) multiplexer_9 (
    .in0(4'b0000), .in1(4'b0111), .out(multiplexer_9_out), .sel(comparator_16_eq));
  Multiplexer #(.width(4)) multiplexer_10 (
    .in0(4'b0000), .in1(4'b1000), .out(multiplexer_10_out), .sel(comparator_17_eq));
  or or_6 (is_j2, and_1_out, or_7_out);
  or or_7 (or_7_out, and_3_out, and_6_out);
  Comparator #(.mode("unsigned"), .width(6)) comparator_21 (
    .a(6'b000011), .b(Inst[31:26]), .eq(comparator_21_eq));  // open: gt, lt
  nor nor_1 (reg_write_e, or_4_out, or_1_out);
  Comparator #(.mode("unsigned"), .width(6)) comparator_22 (
    .a(6'b001001), .b(Inst[5:0]), .eq(comparator_22_eq));  // open: gt, lt
  or or_8 (is_j3, and_1_out, or_9_out);
  or or_9 (or_9_out, comparator_21_eq, and_3_out);
  and and_3 (and_3_out, comparator_22_eq, comparator_2_eq);
  Comparator #(.width(6)) comparator_23 (.a({6{1'b0}}), .b(Inst[5:0]), .eq(comparator_23_eq));  // open: gt, lt
  and and_4 (and_4_out, comparator_23_eq, comparator_20_eq);
  and and_5 (and_5_out, comparator_20_eq, comparator_24_eq);
  Comparator #(.width(6)) comparator_24 (.a(6'b000010), .b(Inst[5:0]), .eq(comparator_24_eq));  // open: gt, lt
  and and_6 (and_6_out, comparator_25_eq, comparator_2_eq);
  Comparator #(.mode("unsigned"), .width(6)) comparator_25 (
    .a(6'b001000), .b(Inst[5:0]), .eq(comparator_25_eq));  // open: gt, lt
  or or_10 (or_10_out, and_4_out, and_5_out);
  assign or_11_out = multiplexer_2_out | multiplexer_3_out | multiplexer_4_out | multiplexer_5_out | multiplexer_6_out | multiplexer_7_out | multiplexer_8_out | multiplexer_9_out | multiplexer_10_out;  // OR_Gate or_11, 4 bits wide
  and and_7 (and_7_out, ~comparator_3_eq, or_10_out);  // AND_Gate
  Multiplexer #(.width(5)) multiplexer_11 (
    .in0(Inst[15:11]), .in1(Inst[20:16]), .out(multiplexer_11_out), .sel(comparator_3_eq));
  assign bit_extender_1_out = {{16{Inst[15]}}, Inst[15:0]};  // Bit_Extender bit_extender_1
  assign bit_extender_2_out = {{27{1'b0}}, Inst[10:6]};  // Bit_Extender bit_extender_2
  or or_12 (or_12_out, comparator_3_eq, and_7_out);
  Multiplexer #(.width(4)) multiplexer_12 (.in0(4'b0000), .in1(4'b1001), .out(multiplexer_12_out), .sel(or_2_out));
  or or_13 (or_13_out, is_j3, is_j2, is_j1, is_beq, is_bne, is_lw, is_sw);
  Multiplexer #(.width(5)) multiplexer_13 (.in0(multiplexer_11_out), .in1(Inst[20:16]), .out(rd), .sel(is_lw));
  Multiplexer #(.width(32)) multiplexer_14 (
    .in0(bit_extender_1_out), .in1(bit_extender_2_out), .out(imm), .sel(and_7_out));
  or or_14 (imm_sel, or_12_out, or_3_out);
  or or_15 (or_15_out, is_lw, is_sw);
  Multiplexer #(.width(5)) multiplexer_15 (.in0(Inst[25:21]), .in1(Inst[20:16]), .out(rs), .sel(and_8_out));
  and and_8 (and_8_out, and_7_out, ~or_15_out);  // AND_Gate
  Multiplexer #(.width(4)) multiplexer_16 (.in0(or_11_out), .in1(multiplexer_12_out), .out(ALU_code), .sel(or_13_out));

  assign rt = Inst[20:16];

  // Notes on the sheet:
  //   opcode
  //   rs
  //   rt
  //   rd
  //   zeros
  //   funccode
  //   sub
  //   mult
  //   div
  //   sll
  //   srl
  //   slt
  //   mfhi
  //   mflo
  //   add
  //   j or jal
  //   j
  //   jal
  //   jalr or jr
  //   jal or jalr
  //   jalr
  //   jr
endmodule

module to7seg (
  input  [3:0] binnum,
  output top,
  output topright,
  output botright,
  output bot,
  output botleft,
  output topleft,
  output middle
);

  wire and_1_out, and_2_out, and_3_out, and_4_out, and_5_out, and_6_out, and_7_out, and_8_out, and_9_out,
       and_10_out, and_11_out, and_12_out, not_1_out, not_2_out, not_3_out, not_4_out, xor_1_out, xor_2_out;

  not not_1 (not_1_out, binnum[3]);
  not not_2 (not_2_out, binnum[2]);
  not not_3 (not_3_out, binnum[1]);
  not not_4 (not_4_out, binnum[0]);
  and and_1 (and_1_out, binnum[2], not_3_out, binnum[0]);
  and and_2 (and_2_out, not_2_out, binnum[1]);
  and and_3 (and_3_out, not_2_out, not_4_out);
  and and_4 (and_4_out, binnum[1], not_4_out);
  and and_5 (and_5_out, not_2_out, not_4_out);
  and and_6 (and_6_out, binnum[1], not_4_out);
  and and_7 (and_7_out, binnum[2], not_3_out);
  and and_8 (and_8_out, not_3_out, not_4_out);
  and and_9 (and_9_out, binnum[2], not_4_out);
  and and_10 (and_10_out, not_2_out, binnum[1]);
  and and_11 (and_11_out, binnum[1], not_4_out);
  and and_12 (and_12_out, binnum[2], not_3_out);
  xor xor_1 (xor_1_out, binnum[2], binnum[0]);
  xor xor_2 (xor_2_out, binnum[1], binnum[0]);
  or or_1 (topright, ~xor_2_out, not_2_out);  // OR_Gate
  or or_2 (bot, and_1_out, and_2_out, and_3_out, and_4_out);
  or or_3 (botleft, and_5_out, and_6_out);
  or or_4 (top, ~xor_1_out, binnum[3], binnum[1]);  // OR_Gate
  or or_5 (botright, binnum[2], not_3_out, binnum[0]);
  or or_6 (topleft, and_7_out, and_8_out, and_9_out, binnum[3]);
  or or_7 (middle, and_10_out, and_11_out, and_12_out, binnum[3]);
  _7_Segment_Display u_7_segment_display_1 (
    .g(middle), .f(topleft), .a(top), .b(topright), .e(botleft), .d(bot), .c(botright));  // open: dp
endmodule

module controller7seg (
  input  [25:0] AddFromBus,
  input  [31:0] DataFromBus,
  output [3:0] out_3,
  output [3:0] out_4,
  output [3:0] out_5
);

  wire clock_1_out, clock_2_out, clock_3_out, comparator_1_eq, comparator_2_eq;
  wire [3:0] binary_to_bcd_converter_1_p2, binary_to_bcd_converter_1_p3, binary_to_bcd_converter_1_p4;
  wire [8:0] bit_extender_1_out;

  Comparator #(.width(26)) comparator_1 (.a(AddFromBus), .b(26'h3ffff30), .eq(comparator_1_eq));  // open: gt, lt
  Comparator #(.width(26)) comparator_2 (.a(AddFromBus), .b(26'h3ffff34), .eq(comparator_2_eq));  // open: gt, lt
  Bit_Extender #(.in_width(32), .out_width(9)) bit_extender_1 (.in(DataFromBus), .out(bit_extender_1_out));
  // Binary_to_BCD_converter binary_to_bcd_converter_1: pin names not known; wires that end beside it: bit_extender_1_out, binary_to_bcd_converter_1_p2, binary_to_bcd_converter_1_p3, binary_to_bcd_converter_1_p4
  Register #(.width(4)) register_1 (
    .D(binary_to_bcd_converter_1_p2), .en(comparator_1_eq), .clk(clock_1_out), .Q(out_3),
    .clr(comparator_2_eq));
  Clock clock_1 (.out(clock_1_out));
  Register #(.width(4)) register_2 (
    .D(binary_to_bcd_converter_1_p3), .en(comparator_1_eq), .clk(clock_2_out), .Q(out_4),
    .clr(comparator_2_eq));
  Clock clock_2 (.out(clock_2_out));
  Register #(.width(4)) register_3 (
    .D(binary_to_bcd_converter_1_p4), .en(comparator_1_eq), .clk(clock_3_out), .Q(out_5),
    .clr(comparator_2_eq));
  Clock clock_3 (.out(clock_3_out));
endmodule

module ledcontroller (
  input  [3:0] in_1,
  input  [3:0] in_2,
  output [14:0] out_3,
  output [14:0] out_4,
  output [14:0] out_5,
  output [14:0] out_6,
  output [14:0] out_7,
  output [14:0] out_8,
  output [14:0] out_9,
  output [14:0] out_10,
  output [14:0] out_11,
  output [14:0] out_12,
  output [14:0] out_13,
  output [14:0] out_14,
  output [14:0] out_15,
  output [14:0] out_16,
  output [14:0] out_17
);

  wire [0:0] not_28_out;
  wire [1:0] not_25_out;
  wire [1:1] not_27_out;
  wire [2:0] not_17_out, not_22_out;
  wire [2:1] not_20_out;
  wire [2:2] not_24_out;
  wire [3:0] not_4_out, not_9_out, not_14_out;
  wire [3:1] not_1_out, not_12_out;
  wire [3:2] not_7_out;
  wire [3:3] not_16_out;
  wire [14:0] and_15_out;

  and and_1 (and_15_out[14], in_1[3], in_1[2], in_1[1], in_1[0]);
  and and_2 (and_15_out[13], in_1[3], in_1[2], in_1[1], ~in_1[0]);  // AND_Gate
  and and_3 (and_15_out[12], in_1[3], in_1[2], ~in_1[1], in_1[0]);  // AND_Gate
  and and_4 (and_15_out[11], in_1[3], in_1[2], ~in_1[1], ~in_1[0]);  // AND_Gate
  and and_5 (and_15_out[10], in_1[3], ~in_1[2], in_1[1], in_1[0]);  // AND_Gate
  and and_6 (and_15_out[9], in_1[3], ~in_1[2], in_1[1], ~in_1[0]);  // AND_Gate
  and and_7 (and_15_out[8], in_1[3], ~in_1[2], ~in_1[1], in_1[0]);  // AND_Gate
  and and_8 (and_15_out[7], in_1[3], ~in_1[2], ~in_1[1], ~in_1[0]);  // AND_Gate
  and and_9 (and_15_out[6], ~in_1[3], in_1[2], in_1[1], in_1[0]);  // AND_Gate
  and and_10 (and_15_out[5], ~in_1[3], in_1[2], in_1[1], ~in_1[0]);  // AND_Gate
  and and_11 (and_15_out[4], ~in_1[3], in_1[2], ~in_1[1], in_1[0]);  // AND_Gate
  and and_12 (and_15_out[3], ~in_1[3], in_1[2], ~in_1[1], ~in_1[0]);  // AND_Gate
  and and_13 (and_15_out[2], ~in_1[3], ~in_1[2], in_1[1], in_1[0]);  // AND_Gate
  and and_14 (and_15_out[1], ~in_1[3], ~in_1[2], in_1[1], ~in_1[0]);  // AND_Gate
  and and_15 (and_15_out[0], ~in_1[3], ~in_1[2], ~in_1[1], in_1[0]);  // AND_Gate
  not not_1 (not_1_out[1], in_2[1]);
  not not_2 (not_1_out[2], in_2[2]);
  not not_3 (not_1_out[3], in_2[3]);
  not not_4 (not_4_out[0], in_2[0]);
  not not_5 (not_4_out[2], in_2[2]);
  not not_6 (not_4_out[3], in_2[3]);
  not not_7 (not_7_out[2], in_2[2]);
  not not_8 (not_7_out[3], in_2[3]);
  not not_9 (not_9_out[0], in_2[0]);
  not not_10 (not_9_out[1], in_2[1]);
  not not_11 (not_9_out[3], in_2[3]);
  not not_12 (not_12_out[1], in_2[1]);
  not not_13 (not_12_out[3], in_2[3]);
  not not_14 (not_14_out[0], in_2[0]);
  not not_15 (not_14_out[3], in_2[3]);
  not not_16 (not_16_out[3], in_2[3]);
  not not_17 (not_17_out[0], in_2[0]);
  not not_18 (not_17_out[1], in_2[1]);
  not not_19 (not_17_out[2], in_2[2]);
  not not_20 (not_20_out[1], in_2[1]);
  not not_21 (not_20_out[2], in_2[2]);
  not not_22 (not_22_out[0], in_2[0]);
  not not_23 (not_22_out[2], in_2[2]);
  not not_24 (not_24_out[2], in_2[2]);
  not not_25 (not_25_out[0], in_2[0]);
  not not_26 (not_25_out[1], in_2[1]);
  not not_27 (not_27_out[1], in_2[1]);
  not not_28 (not_28_out[0], in_2[0]);
  ledsub ledsub_1 (.in_1(and_15_out), .in_2({not_1_out, in_2[0]}), .out_3(out_3));
  ledsub ledsub_2 (.in_1(and_15_out), .in_2({not_4_out[3:2], in_2[1], not_4_out[0]}), .out_3(out_4));
  ledsub ledsub_3 (.in_1(and_15_out), .in_2({not_7_out, in_2[1:0]}), .out_3(out_5));
  ledsub ledsub_4 (.in_1(and_15_out), .in_2({not_9_out[3], in_2[2], not_9_out[1:0]}), .out_3(out_6));
  ledsub ledsub_5 (.in_1(and_15_out), .in_2({not_12_out[3], in_2[2], not_12_out[1], in_2[0]}), .out_3(out_7));
  ledsub ledsub_6 (.in_1(and_15_out), .in_2({not_14_out[3], in_2[2:1], not_14_out[0]}), .out_3(out_8));
  ledsub ledsub_7 (.in_1(and_15_out), .in_2({not_16_out[3], in_2[2:0]}), .out_3(out_9));
  ledsub ledsub_8 (.in_1(and_15_out), .in_2({in_2[3], not_17_out}), .out_3(out_10));
  ledsub ledsub_9 (.in_1(and_15_out), .in_2({in_2[3], not_20_out, in_2[0]}), .out_3(out_11));
  ledsub ledsub_10 (.in_1(and_15_out), .in_2({in_2[3], not_22_out[2], in_2[1], not_22_out[0]}), .out_3(out_12));
  ledsub ledsub_11 (.in_1(and_15_out), .in_2({in_2[3], not_24_out[2], in_2[1:0]}), .out_3(out_13));
  ledsub ledsub_12 (.in_1(and_15_out), .in_2({in_2[3:2], not_25_out}), .out_3(out_14));
  ledsub ledsub_13 (.in_1(and_15_out), .in_2({in_2[3:2], not_27_out[1], in_2[0]}), .out_3(out_15));
  ledsub ledsub_14 (.in_1(and_15_out), .in_2({in_2[3:1], not_28_out[0]}), .out_3(out_16));
  ledsub ledsub_15 (.in_1(and_15_out), .in_2(in_2), .out_3(out_17));
endmodule

module ledsub (
  input  [14:0] in_1,
  input  [3:0] in_2,
  output [14:0] out_3
);

  wire and_1_out, and_2_out, and_3_out, and_4_out, and_5_out, and_6_out, and_7_out, and_8_out, and_9_out,
       and_10_out, and_11_out, and_12_out, and_13_out, and_14_out, and_15_out, and_16_out, and_17_out,
       and_18_out, and_19_out, and_20_out, and_21_out, and_22_out, and_23_out, and_24_out, and_25_out,
       and_26_out, and_27_out, and_28_out, and_29_out, and_30_out, and_31_out, and_32_out, and_33_out,
       and_34_out, and_35_out, and_36_out, and_37_out, and_38_out, and_39_out, and_40_out, and_41_out,
       and_42_out, and_43_out, and_44_out, and_45_out;

  and and_1 (and_1_out, in_2[0], in_2[1]);
  and and_2 (and_2_out, in_2[2], in_2[3]);
  and and_3 (and_3_out, in_2[0], in_2[1]);
  and and_4 (and_4_out, in_2[2], in_2[3]);
  and and_5 (and_5_out, in_2[0], in_2[1]);
  and and_6 (and_6_out, in_2[2], in_2[3]);
  and and_7 (and_7_out, in_2[0], in_2[1]);
  and and_8 (and_8_out, in_2[2], in_2[3]);
  and and_9 (and_9_out, in_2[0], in_2[1]);
  and and_10 (and_10_out, in_2[2], in_2[3]);
  and and_11 (and_11_out, in_2[0], in_2[1]);
  and and_12 (and_12_out, in_2[2], in_2[3]);
  and and_13 (and_13_out, in_2[0], in_2[1]);
  and and_14 (and_14_out, in_2[2], in_2[3]);
  and and_15 (and_15_out, in_2[0], in_2[1]);
  and and_16 (and_16_out, in_2[2], in_2[3]);
  and and_17 (and_17_out, in_2[0], in_2[1]);
  and and_18 (and_18_out, in_2[2], in_2[3]);
  and and_19 (and_19_out, in_2[0], in_2[1]);
  and and_20 (and_20_out, in_2[2], in_2[3]);
  and and_21 (and_21_out, in_2[0], in_2[1]);
  and and_22 (and_22_out, in_2[2], in_2[3]);
  and and_23 (and_23_out, in_2[0], in_2[1]);
  and and_24 (and_24_out, in_2[2], in_2[3]);
  and and_25 (and_25_out, in_2[0], in_2[1]);
  and and_26 (and_26_out, in_2[2], in_2[3]);
  and and_27 (and_27_out, in_2[0], in_2[1]);
  and and_28 (and_28_out, in_2[2], in_2[3]);
  and and_29 (and_29_out, in_2[0], in_2[1]);
  and and_30 (and_30_out, in_2[2], in_2[3]);
  and and_31 (and_31_out, and_1_out, and_2_out);
  and and_32 (and_32_out, and_3_out, and_4_out);
  and and_33 (and_33_out, and_5_out, and_6_out);
  and and_34 (and_34_out, and_7_out, and_8_out);
  and and_35 (and_35_out, and_9_out, and_10_out);
  and and_36 (and_36_out, and_11_out, and_12_out);
  and and_37 (and_37_out, and_13_out, and_14_out);
  and and_38 (and_38_out, and_15_out, and_16_out);
  and and_39 (and_39_out, and_17_out, and_18_out);
  and and_40 (and_40_out, and_19_out, and_20_out);
  and and_41 (and_41_out, and_21_out, and_22_out);
  and and_42 (and_42_out, and_23_out, and_24_out);
  and and_43 (and_43_out, and_25_out, and_26_out);
  and and_44 (and_44_out, and_27_out, and_28_out);
  and and_45 (and_45_out, and_29_out, and_30_out);
  and and_46 (out_3[0], in_1[14], and_31_out);
  and and_47 (out_3[1], in_1[13], and_32_out);
  and and_48 (out_3[2], in_1[12], and_33_out);
  and and_49 (out_3[3], in_1[11], and_34_out);
  and and_50 (out_3[4], in_1[10], and_35_out);
  and and_51 (out_3[5], in_1[9], and_36_out);
  and and_52 (out_3[6], in_1[8], and_37_out);
  and and_53 (out_3[7], in_1[7], and_38_out);
  and and_54 (out_3[8], in_1[6], and_39_out);
  and and_55 (out_3[9], in_1[5], and_40_out);
  and and_56 (out_3[10], in_1[4], and_41_out);
  and and_57 (out_3[11], in_1[3], and_42_out);
  and and_58 (out_3[12], in_1[2], and_43_out);
  and and_59 (out_3[13], in_1[1], and_44_out);
  and and_60 (out_3[14], in_1[0], and_45_out);
endmodule

module joycontrol (
  input  [25:0] address,
  input  [31:0] data,
  output [31:0] data_tobus,
  output we_tobus
);

  Comparator #(.width(26)) comparator_1 (.a(address), .b(26'h3ffff38), .eq(we_tobus));  // open: gt, lt
  assign data_tobus = we_tobus ? data : 32'bz;  // Controlled_Buffer controlled_buffer_1
endmodule

module matrixcontroller (
  input  WriteEnableFromBus,
  input  [25:0] AddressFromBus,
  input  [31:0] DataFromBus,
  output [14:0] out_4,
  output [14:0] out_5,
  output [14:0] out_6,
  output [14:0] out_7,
  output [14:0] out_8,
  output [14:0] out_9,
  output [14:0] out_10,
  output [14:0] out_11,
  output [14:0] out_12,
  output [14:0] out_13,
  output [14:0] out_14,
  output [14:0] out_15,
  output [14:0] out_16,
  output [14:0] out_17,
  output [14:0] out_18
);

  wire and_1_out, clock_1_out, clock_2_out, clock_3_out, clock_4_out, clock_5_out, clock_6_out, clock_7_out,
       clock_8_out, clock_9_out, clock_10_out, clock_11_out, clock_12_out, clock_13_out, clock_14_out,
       clock_15_out, comparator_1_eq;
  wire [14:0] ledcontroller_1_out_3, ledcontroller_1_out_4, ledcontroller_1_out_5, ledcontroller_1_out_6,
       ledcontroller_1_out_7, ledcontroller_1_out_8, ledcontroller_1_out_9, ledcontroller_1_out_10,
       ledcontroller_1_out_11, ledcontroller_1_out_12, ledcontroller_1_out_13, ledcontroller_1_out_14,
       ledcontroller_1_out_15, ledcontroller_1_out_16, ledcontroller_1_out_17;
  wire [31:0] controlled_buffer_1_out;

  Comparator #(.mode("unsigned"), .width(26)) comparator_1 (
    .a(AddressFromBus), .b(26'h3ffff3c), .eq(comparator_1_eq));  // open: gt, lt
  and and_1 (and_1_out, WriteEnableFromBus, comparator_1_eq);
  assign controlled_buffer_1_out = and_1_out ? DataFromBus : 32'bz;  // Controlled_Buffer controlled_buffer_1
  ledcontroller ledcontroller_1 (
    .in_1(controlled_buffer_1_out[3:0]), .in_2(controlled_buffer_1_out[7:4]), .out_3(ledcontroller_1_out_3),
    .out_4(ledcontroller_1_out_4), .out_5(ledcontroller_1_out_5), .out_6(ledcontroller_1_out_6),
    .out_7(ledcontroller_1_out_7), .out_8(ledcontroller_1_out_8), .out_9(ledcontroller_1_out_9),
    .out_10(ledcontroller_1_out_10), .out_11(ledcontroller_1_out_11), .out_12(ledcontroller_1_out_12),
    .out_13(ledcontroller_1_out_13), .out_14(ledcontroller_1_out_14), .out_15(ledcontroller_1_out_15),
    .out_16(ledcontroller_1_out_16), .out_17(ledcontroller_1_out_17));
  Register #(.width(15)) register_1 (
    .D(ledcontroller_1_out_3), .en(and_1_out), .clk(clock_1_out), .Q(out_4));  // open: clr
  Clock clock_1 (.out(clock_1_out));
  Register #(.width(15)) register_2 (
    .D(ledcontroller_1_out_4), .en(and_1_out), .clk(clock_2_out), .Q(out_5));  // open: clr
  Clock clock_2 (.out(clock_2_out));
  Register #(.width(15)) register_3 (
    .D(ledcontroller_1_out_5), .en(and_1_out), .clk(clock_3_out), .Q(out_6));  // open: clr
  Clock clock_3 (.out(clock_3_out));
  Register #(.width(15)) register_4 (
    .D(ledcontroller_1_out_6), .en(and_1_out), .clk(clock_4_out), .Q(out_7));  // open: clr
  Clock clock_4 (.out(clock_4_out));
  Register #(.width(15)) register_5 (
    .D(ledcontroller_1_out_7), .en(and_1_out), .clk(clock_5_out), .Q(out_8));  // open: clr
  Clock clock_5 (.out(clock_5_out));
  Register #(.width(15)) register_6 (
    .D(ledcontroller_1_out_8), .en(and_1_out), .clk(clock_6_out), .Q(out_9));  // open: clr
  Clock clock_6 (.out(clock_6_out));
  Register #(.width(15)) register_7 (
    .D(ledcontroller_1_out_9), .en(and_1_out), .clk(clock_7_out), .Q(out_10));  // open: clr
  Clock clock_7 (.out(clock_7_out));
  Register #(.width(15)) register_8 (
    .D(ledcontroller_1_out_10), .en(and_1_out), .clk(clock_8_out), .Q(out_11));  // open: clr
  Clock clock_8 (.out(clock_8_out));
  Register #(.width(15)) register_9 (
    .D(ledcontroller_1_out_11), .en(and_1_out), .clk(clock_9_out), .Q(out_12));  // open: clr
  Clock clock_9 (.out(clock_9_out));
  Register #(.width(15)) register_10 (
    .D(ledcontroller_1_out_12), .en(and_1_out), .clk(clock_10_out), .Q(out_13));  // open: clr
  Clock clock_10 (.out(clock_10_out));
  Register #(.width(15)) register_11 (
    .D(ledcontroller_1_out_13), .en(and_1_out), .clk(clock_11_out), .Q(out_14));  // open: clr
  Clock clock_11 (.out(clock_11_out));
  Register #(.width(15)) register_12 (
    .D(ledcontroller_1_out_14), .en(and_1_out), .clk(clock_12_out), .Q(out_15));  // open: clr
  Clock clock_12 (.out(clock_12_out));
  Register #(.width(15)) register_13 (
    .D(ledcontroller_1_out_15), .en(and_1_out), .clk(clock_13_out), .Q(out_16));  // open: clr
  Clock clock_13 (.out(clock_13_out));
  Register #(.width(15)) register_14 (
    .D(ledcontroller_1_out_16), .en(and_1_out), .clk(clock_14_out), .Q(out_17));  // open: clr
  Clock clock_14 (.out(clock_14_out));
  Register #(.width(15)) register_15 (
    .D(ledcontroller_1_out_17), .en(and_1_out), .clk(clock_15_out), .Q(out_18));  // open: clr
  Clock clock_15 (.out(clock_15_out));
endmodule
